// Logisim project InfoIIUebung1.circ as structural Verilog
module NOT_Gatter (
  input  in_1,
  output out_2
);

  nand nand_1 (out_2, in_1, 1'b1);
endmodule

module AND_Gatter (
  input  in_1,
  input  in_2,
  output out_3
);

  wire nand_1_out, nand_2_out;

  nand nand_1 (nand_1_out, in_1, in_2);
  nand nand_2 (nand_2_out, in_1, in_2);
  nand nand_3 (out_3, nand_1_out, nand_2_out);
endmodule

module OR_Gatter (
  input  in_1,
  input  in_2,
  output out_3
);

  wire nand_1_out, nand_2_out;

  nand nand_1 (nand_1_out, in_1, in_1);
  nand nand_2 (nand_2_out, in_2, in_2);
  nand nand_3 (out_3, nand_1_out, nand_2_out);
endmodule

module MUX (
  input  in_1,
  input  in_2,
  output out_3
);

  wire and_1_out, and_2_out, not_1_out;

  not not_1 (not_1_out, 1'b1);
  and and_1 (and_1_out, in_1, not_1_out);
  and and_2 (and_2_out, 1'b1, in_2);
  or or_1 (out_3, and_1_out, and_2_out);
endmodule
